# Fritzing sketch breadboard (saved by Fritzing 0.9.3b)
breadboards: 4

parts:
  Microcontroller = IC, DIP package, 40 pins [chip_label="Atmega 162"]
  RESET = Pushbutton [package="[SMD]"]
  LED = LED - 3mm [color="Red (633nm)" package="3 mm [THT]"]
  C3 = Capacitor [package=cap-pth-small]
  U1 = Voltage Regulator - 5V [package="TO220 [THT]"]
  Clock = Crystal [frequency="4 MHz" package=THT]
  RS232 = IC, DIP package, 20 pins [chip_label=MAX233]
  UART_connector = male pin header, 5 pins [form="♂ (male)"]
  CAN_controller = IC, DIP package, 18 pins [chip_label=MCP2515]
  C2 = Capacitor [package=cap-pth-large]
  CAN_trancv = IC, DIP package, 8 pins [chip_label=MC2551]
  Latch = IC, DIP package, 20 pins [chip_label=SN74ALS573C]
  ADC = DIP - 20 pins [chip_label=ADC0844CCN package="DIP (Dual Inline) [THT]"]
  SRAM = IC, DIP package, 28 pins [chip_label="SRAM IDT_7164SL"]
  GAL = IC, DIP package, 20 pins [chip_label=GAL16V8D]
  C7 = Ceramic Capacitor [capacitance="100 nF" package="0603 [SMD, multilayer]"]
  JTAG = male pin header, 4 pins [form="♂ (male)"]
  C8 = Capacitor [package=cap-pth-large]
  Game_board = male pin header, 16 pins [form="♂ (male)"]
  Game_board_buttons = male pin header, 3 pins [form="♂ (male)"]
  C9 = Capacitor [package=cap-pth-large]
  C11 = Capacitor [package=cap-pth-small2]
  Clock1 = Crystal [frequency="16 MHz" package=THT]
  C12 = Capacitor [package=cap-pth-large]
  Terminate_CAN = Resistor [tolerance=±5% resistance=120 package="0402 [SMD]"]
  CAN_bus = male pin header, 2 pins [form="♂ (male)"]
  C13 = Capacitor [package=cap-pth-large]
  Reset_CAN = Resistor [tolerance=±5% resistance=22k package="0402 [SMD]"]
  VCC1 = Battery block 9V
  Reset_Atmega = Resistor [tolerance=±5% resistance=22k package="0402 [SMD]"]
  C14 = Capacitor [package=cap-pth-large]
  C15 = Capacitor [package=cap-pth-small2]
  Reset_NCP = Capacitor [package=cap-pth-large]
  Jtag_Pow = male pin header, 2 pins [form="♂ (male)"]
  RS_resistor = Resistor [tolerance=±5% resistance=22k package="0402 [SMD]"]
  JTAG_Power = male pin header, 1 pin [form="♂ (male)"]

nets:
  N1: Microcontroller.pin1, LED.anode
  PB1: Microcontroller.pin2, Game_board_buttons.pin3
  PB2: Microcontroller.pin3, Game_board_buttons.pin2
  PB3: Microcontroller.pin4, Game_board_buttons.pin1
  PB4: Microcontroller.pin5, CAN_controller.pin16
  PB5: Microcontroller.pin6, CAN_controller.pin14
  PB6: Microcontroller.pin7, CAN_controller.pin15
  PB7: Microcontroller.pin8, CAN_controller.pin13
  RESET: Microcontroller.pin9, RESET.Pin_1, RESET.Pin_2, CAN_controller.pin17, Reset_CAN.Pin_1, Reset_Atmega.Pin_1, Reset_NCP.1
  Rx: Microcontroller.pin10, RS232.pin3
  Tx: Microcontroller.pin11, RS232.pin2
  !WR: Microcontroller.pin16, ADC.!WR, SRAM.pin27, Game_board.pin7
  !RD: Microcontroller.pin17, ADC.!RD, SRAM.pin22, C15.2
  N2: Microcontroller.pin18, Clock.pin_1
  N3: Microcontroller.pin19, Clock.pin_0, C14.2, C15.1
  GND: Microcontroller.pin20, RESET.Pin_3, RESET.Pin_4, LED.cathode, C3.2, U1.GND, RS232.pin6, C2.2, CAN_trancv.pin2, Latch.pin1, Latch.pin10, ADC.AGND, ADC.DGND, SRAM.pin2, SRAM.pin14, GAL.pin10, C7.0, C8.2, Game_board.pin16, C9.1, C13.1, C14.1, Reset_NCP.2, Jtag_Pow.pin1, Jtag_Pow.pin2, RS_resistor.Pin_0
  A11: Microcontroller.pin21, SRAM.pin23, GAL.pin4
  A10: Microcontroller.pin22, SRAM.pin21, GAL.pin3
  A9: Microcontroller.pin23, SRAM.pin24, GAL.pin2
  A8: Microcontroller.pin24, SRAM.pin25, GAL.pin1
  JTAG4: Microcontroller.pin25, JTAG.pin1
  JTAG3: Microcontroller.pin26, JTAG.pin2
  JTAG2: Microcontroller.pin27, JTAG.pin3
  JTAG1: Microcontroller.pin28, JTAG.pin4
  LE: Microcontroller.pin30, Latch.pin11
  data7: Microcontroller.pin32, Latch.pin9, ADC.DB7, SRAM.pin19, Game_board.pin15
  data6: Microcontroller.pin33, Latch.pin8, ADC.DB6, SRAM.pin18, Game_board.pin14
  data5: Microcontroller.pin34, Latch.pin7, ADC.DB5, SRAM.pin17, Game_board.pin13
  data4: Microcontroller.pin35, Latch.pin6, ADC.DB4, SRAM.pin16, Game_board.pin12
  data3: Microcontroller.pin36, Latch.pin5, ADC.DB3, SRAM.pin15, Game_board.pin11
  data2: Microcontroller.pin37, Latch.pin4, ADC.DB2, SRAM.pin13, Game_board.pin10
  data1: Microcontroller.pin38, Latch.pin3, ADC.DB1, SRAM.pin12, Game_board.pin9
  data0: Microcontroller.pin39, Latch.pin2, ADC.DB0, SRAM.pin11, Game_board.pin8
  N4: Microcontroller.pin40, C2.1
  N5: C3.1, U1.input_voltage
  5V: U1.output_voltage, RS232.pin7, CAN_controller.pin18, CAN_trancv.pin3, Latch.pin20, ADC.VREF, ADC.VCC, SRAM.pin26, SRAM.pin28, GAL.pin20, C7.1, C8.1, C9.2, C13.2, Reset_CAN.Pin_0, VCC1.-, Reset_Atmega.Pin_0, JTAG_Power.pin1
  R1IN: RS232.pin4, UART_connector.pin3
  T1OUT: RS232.pin5, UART_connector.pin4
  N6: RS232.pin10, RS232.pin16
  N7: RS232.pin11, RS232.pin15
  N8: RS232.pin12, RS232.pin17
  N9: CAN_controller.pin1, CAN_trancv.pin1
  N10: CAN_controller.pin2, CAN_trancv.pin4
  N11: CAN_controller.pin7, C11.1, Clock1.pin_0
  N12: CAN_controller.pin8, Clock1.pin_1, C12.1
  N13: CAN_controller.pin9, C11.2, C12.2
  CANL: CAN_trancv.pin6, Terminate_CAN.Pin_0, CAN_bus.pin2
  CANH: CAN_trancv.pin7, Terminate_CAN.Pin_1, CAN_bus.pin1
  N14: CAN_trancv.pin8, RS_resistor.Pin_1
  dataOut7: Latch.pin12, SRAM.pin3
  dataOut6: Latch.pin13, SRAM.pin4
  dataOut5: Latch.pin14, SRAM.pin5
  dataOut4: Latch.pin15, SRAM.pin6
  dataOut3: Latch.pin16, SRAM.pin7
  dataOut2: Latch.pin17, SRAM.pin8
  dataOut1: Latch.pin18, SRAM.pin9
  dataOut0: Latch.pin19, SRAM.pin10
  !CS_ADC: ADC.!CS, GAL.pin18
  JOYSTICK_R: ADC.CH1, Game_board.pin1
  JOYSTICK_L: ADC.CH2, Game_board.pin2
  SLIDER_R: ADC.CH3, Game_board.pin3
  SLIDER_L: ADC.CH4, Game_board.pin4
  !CS_SRAM: SRAM.pin20, GAL.pin19
  !DC_OLED: GAL.pin16, Game_board.pin6
  !CS_OLED: GAL.pin17, Game_board.pin5

notes:
  POWER SUPPLY, 1
  LATCH, 1
  UART - RS232, 1
  CAN BUS, 1
  JTAG
  RESET
  UART
  STATUS ON/OFF
  GND
  5V
  CS/WR
  Data/Addr
  TX/RX
  OLED/GPIO
  Connectors, 1
  CAN
  GAME BOARD
  JTAG POW

custom parts:
  DIP - 20 pins: A DIP stand-in part for whatever IC you want. With 20 pins on a 300mil dual inline package (DIP) footprint.
